# Fritzing sketch estacionamento1.0 (saved by Fritzing 0.9.3b)
breadboards: 2

parts:
  Componente1 = Arduino Uno (Rev3) - ICSP
  U2 = TCRT5000 [package=THT]
  U3 = TCRT5000 [package=THT]
  U4 = TCRT5000 [package=THT]
  U5 = TCRT5000 [package=THT]
  LED1 = LED - 5mm [color="Green (555nm)" package="5 mm [THT]"]
  LED2 = LED - 5mm [color="Red (633nm)" package="5 mm [THT]"]
  LED3 = LED - 5mm [color="Green (555nm)" package="5 mm [THT]"]
  LED4 = LED - 5mm [color="Red (633nm)" package="5 mm [THT]"]
  LED5 = LED - 5mm [color="Green (555nm)" package="5 mm [THT]"]
  R1 = Resistor [tolerance=±5% resistance=220 package=THT]
  R2 = Resistor [tolerance=±5% resistance=220 package=THT]
  R3 = Resistor [tolerance=±5% resistance=220 package=THT]
  R4 = Resistor [tolerance=±5% resistance=220 package=THT]
  R5 = Resistor [tolerance=±5% resistance=220 package=THT]
  R6 = Resistor [tolerance=±5% resistance=220 package=THT]
  J1 = Basic Servo
  J2 = Basic Servo
  R14 = Resistor [tolerance=±5% resistance=220 package=THT]
  R15 = Resistor [tolerance=±5% resistance=10k package=THT]
  R16 = Resistor [tolerance=±5% resistance=220 package=THT]
  R17 = Resistor [tolerance=±5% resistance=220 package=THT]
  R18 = Resistor [tolerance=±5% resistance=220 package=THT]
  R19 = Resistor [tolerance=±5% resistance=220 package=THT]
  LED6 = LED - 5mm [color="Red (633nm)" package="5 mm [THT]"]
  R20 = Resistor [tolerance=±5% resistance=10k package=THT]
  R21 = Resistor [tolerance=±5% resistance=10k package=THT]
  R22 = Resistor [tolerance=±5% resistance=10k package=THT]
  R23 = Resistor [tolerance=±5% resistance=10k package=THT]
  C2 = Electrolytic Capacitor [capacitance=0.47mF package="200 mil [THT, electrolytic]"]
  C3 = Electrolytic Capacitor [capacitance=0.47mF package="200 mil [THT, electrolytic]"]
  U1 = TCRT5000 [package=THT]
  LCD1 = LCD screen
  R24 = Trimmer Potentiometer [maximum_resistance=10kΩ package=THT]
  R25 = Resistor [tolerance=±5% resistance=220 package=THT]  # not connected
  R26 = Resistor [tolerance=±5% resistance=220 package=THT]

nets:
  N1: Componente1.A0, R15.Pin_0, U1.Pin_4
  N2: Componente1.A1, U2.Pin_4, R20.Pin_0
  N3: Componente1.A2, U3.Pin_4, R21.Pin_0
  N4: Componente1.A3, U4.Pin_4, R22.Pin_0
  N5: Componente1.A4/SDA, U5.Pin_4, R23.Pin_0
  N6: Componente1.ICSP_MISO, Componente1.D12/MISO, LCD1.E
  N7: Componente1.D8, LCD1.DB5
  N8: Componente1.D9_PWM, J1.pulse
  N9: Componente1.D10_PWM/SS, J2.pulse
  N10: Componente1.D11_PWM/MOSI, LCD1.DB4
  N11: Componente1.D13/SCK, LCD1.RS
  N12: Componente1.D0/RX, LCD1.DB7
  N13: Componente1.D1/TX, LCD1.DB6
  N14: Componente1.D2, R1.Pin_0
  N15: Componente1.D3_PWM, R2.Pin_0
  N16: Componente1.D4, R3.Pin_0
  N17: Componente1.D5_PWM, R4.Pin_0
  N18: Componente1.D6_PWM, R5.Pin_0
  N19: Componente1.D7, R6.Pin_0
  VCC: Componente1.5V, J1.vcc, J2.vcc, R14.Pin_1, R15.Pin_1, R16.Pin_1, R17.Pin_1, R18.Pin_1, R19.Pin_1, R20.Pin_1, R21.Pin_1, R22.Pin_1, R23.Pin_1, C2.+, C3.+, LCD1.VDD, R24.leg2, R26.Pin_1
  GND: Componente1.GND, U2.Pin_2, U2.Pin_3, U3.Pin_2, U3.Pin_3, U4.Pin_2, U4.Pin_3, U5.Pin_2, U5.Pin_3, LED1.cathode, LED2.cathode, LED3.cathode, LED4.cathode, LED5.cathode, J1.gnd, LED6.cathode, C2.-, C3.-, U1.Pin_2, U1.Pin_3, LCD1.VSS, LCD1.R/W, LCD1.LED-, R24.leg1
  N20: U2.Pin_1, R16.Pin_0
  N21: U3.Pin_1, R17.Pin_0
  N22: U4.Pin_1, R18.Pin_0
  N23: U5.Pin_1, R19.Pin_0
  N24: LED1.anode, R1.Pin_1
  N25: LED2.anode, R2.Pin_1
  N26: LED3.anode, R3.Pin_1
  N27: LED4.anode, R4.Pin_1
  N28: LED5.anode, R5.Pin_1
  N29: R6.Pin_1, LED6.anode
  N30: R14.Pin_0, U1.Pin_1
  N31: LCD1.V0, R24.wiper
  N32: LCD1.LED+, R26.Pin_0

custom parts:
  TCRT5000: TCRT5000 optical reflective sensor
